# Fritzing sketch sch_bb_pcb (saved by Fritzing 0.8.7b)
breadboards: 1

parts:
  Part1 = Arduino Ethernet Shield (Rev3)
  LED1 = LED - 5mm [color="Red (633nm)" package="5 mm [THT]"]
  R1 = Resistor [tolerance=±5% resistance=220 package=THT]
  Part2 = Arduino Mega ADK (Rev3)

nets:
  N1: Part1.ETH_CS, Part2.D10_PWM
  N2: Part1.SDCS, Part2.D4_PWM
  GND: Part1.GND, R1.Pin_1, Part2.GND
  N3: LED1.cathode, Part2.D13_PWM
  N4: LED1.anode, R1.Pin_0
